// Logisim project Project_1_ECS154A.circ as structural Verilog: 4 circuits, main circuit main
module main (
  input  in_1,
  input  in_2,
  input  in_3,
  input  in_4,
  input  in_5,
  output [3:0] out_6
);

  wire compare_1_e, compare_1_n, fiveseven_1_a, fiveseven_1_b, fiveseven_1_c, fiveseven_1_d, fiveseven_1_e,
       fiveseven_1_f, fiveseven_1_g;

  FiveSeven fiveseven_1 (
    .V(in_1), .W(in_2), .X(in_3), .Y(in_4), .Z(in_5), .A(fiveseven_1_a), .B(fiveseven_1_b),
    .C(fiveseven_1_c), .D(fiveseven_1_d), .E(fiveseven_1_e), .F(fiveseven_1_f), .G(fiveseven_1_g));
  _7_Segment_Display #(.decimalPoint("false")) u_7_segment_display_1 (
    .g(fiveseven_1_g), .f(fiveseven_1_f), .a(fiveseven_1_a), .b(fiveseven_1_b), .e(fiveseven_1_e),
    .d(fiveseven_1_d), .c(fiveseven_1_c));
  LED Equal (.in(compare_1_e));
  Compare compare_1 (
    .X0(1'b0), .X1(1'b0), .X2(1'b0), .Y0(1'b0), .Y1(1'b0), .Y2(1'b0), .E(compare_1_e), .N(compare_1_n));
  LED Not_Equal (.in(compare_1_n));
  Gray gray_1 (.B3(1'b0), .B2(1'b0), .B1(1'b0), .B0(1'b0), .G3(out_6[0]), .G2(out_6[1]), .G1(out_6[2]), .G0(out_6[3]));
endmodule

module Compare (
  input  X0,
  input  X1,
  input  X2,
  input  Y0,
  input  Y1,
  input  Y2,
  output E,
  output N
);

  wire [2:0] xnor_1_out;

  assign xnor_1_out = ~({X2, X1, X0} ^ {Y2, Y1, Y0});  // XNOR_Gate xnor_1, 3 bits wide
  and and_1 (E, xnor_1_out[0], xnor_1_out[1], xnor_1_out[2]);
  not not_1 (N, E);
endmodule

module Gray (
  input  B3,
  input  B2,
  input  B1,
  input  B0,
  output G3,
  output G2,
  output G1,
  output G0
);

  wire and_1_out, and_2_out, and_3_out, and_4_out, and_5_out, and_6_out, and_7_out, and_8_out, and_9_out,
       and_10_out, and_11_out, and_12_out, and_13_out, and_14_out, and_15_out, and_16_out, not_1_out,
       not_2_out, not_3_out, not_4_out;

  not not_1 (not_1_out, B3);
  not not_2 (not_2_out, B2);
  not not_3 (not_3_out, B1);
  not not_4 (not_4_out, B0);
  and and_1 (and_1_out, not_1_out, not_2_out, not_3_out, not_4_out);
  and and_2 (and_2_out, not_1_out, not_2_out, not_3_out, B0);
  and and_3 (and_3_out, not_1_out, not_2_out, B1, not_4_out);
  and and_4 (and_4_out, not_1_out, not_2_out, B1, B0);
  and and_5 (and_5_out, not_1_out, B2, not_3_out, not_4_out);
  and and_6 (and_6_out, not_1_out, B2, not_3_out, B0);
  and and_7 (and_7_out, not_1_out, B2, B1, not_4_out);
  and and_8 (and_8_out, not_1_out, B2, B1, B0);
  and and_9 (and_9_out, B3, not_2_out, not_3_out, not_4_out);
  and and_10 (and_10_out, B3, not_1_out, not_3_out, B0);
  and and_11 (and_11_out, B3, not_2_out, B1, not_4_out);
  and and_12 (and_12_out, B3, not_2_out, B1, B0);
  and and_13 (and_13_out, B3, B2, not_3_out, not_4_out);
  and and_14 (and_14_out, B3, B2, not_3_out, B0);
  and and_15 (and_15_out, B3, B2, B1, not_4_out);
  and and_16 (and_16_out, B3, B2, B1, B0);
  or or_1 (G3, and_2_out, and_3_out, and_4_out, and_5_out, and_6_out, and_7_out, and_8_out, and_9_out, and_10_out);
  or or_2 (G2, and_1_out, and_2_out, and_3_out, and_4_out, and_5_out, and_14_out, and_15_out, and_16_out, and_10_out);
  or or_3 (G1, and_15_out, and_4_out, and_5_out, and_6_out, and_7_out, and_12_out, and_13_out, and_14_out, and_10_out);
  or or_4 (G0, and_4_out, and_15_out, and_7_out, and_8_out, and_11_out, and_12_out, and_3_out, and_16_out, and_10_out);
  // also tied to GND on the sheet: and_10_out
endmodule

module FiveSeven (
  input  V,
  input  W,
  input  X,
  input  Y,
  input  Z,
  output A,
  output B,
  output C,
  output D,
  output E,
  output F,
  output G
);

  wire and_7_out, and_9_out, and_10_out, and_12_out, and_14_out, Eight, Five, Four, Nine, nor_1_out, One,
       or_1_out, or_2_out, or_3_out, or_4_out, or_5_out, or_6_out, Seven, Six, Three, Two, xor_1_out,
       xor_2_out, xor_3_out, xor_4_out, xor_5_out, xor_6_out, Zero;

  and and_1 (Five, nor_1_out, Z);
  and and_2 (Zero, ~Z, nor_1_out);  // AND_Gate
  nor nor_1 (nor_1_out, V, Y, X, W);
  and and_3 (Six, Z, xor_1_out);
  and and_4 (One, ~Z, xor_1_out);  // AND_Gate
  ExactlyOne xor_1 (.out(xor_1_out), .in0(W), .in1(X), .in2(Y), .in3(V));
  and and_5 (Two, ~Z, xor_4_out);  // AND_Gate
  or or_1 (or_1_out, V, W);
  or or_2 (or_2_out, X, Y);
  xor xor_2 (xor_2_out, or_1_out, or_2_out);
  or or_3 (or_3_out, V, X);
  or or_4 (or_4_out, W, Y);
  xor xor_3 (xor_3_out, or_3_out, or_4_out);
  ExactlyOne xor_4 (.out(xor_4_out), .in0(xor_2_out), .in1(xor_3_out), .in2(xor_5_out));
  and and_6 (Seven, Z, xor_4_out);
  or or_5 (or_5_out, V, Y);
  or or_6 (or_6_out, W, X);
  xor xor_5 (xor_5_out, or_5_out, or_6_out);
  and and_7 (and_7_out, V, W, X);
  and and_8 (Three, ~Z, xor_6_out);  // AND_Gate
  and and_9 (and_9_out, W, X, Y);
  and and_10 (and_10_out, V, X, Y);
  ExactlyOne xor_6 (.out(xor_6_out), .in0(and_7_out), .in1(and_9_out), .in2(and_10_out), .in3(and_12_out));
  and and_11 (Eight, Z, xor_6_out);
  and and_12 (and_12_out, V, W, Y);
  and and_13 (Nine, Z, and_14_out);
  and and_14 (and_14_out, Y, X, W, V);
  and and_15 (Four, ~Z, and_14_out);  // AND_Gate
  or or_7 (A, Zero, Two, Three, Five, Six, Seven, Eight, Nine);
  or or_8 (B, Zero, One, Two, Three, Four, Seven, Eight, Nine);
  or or_9 (C, Zero, One, Three, Four, Five, Six, Seven, Eight, Nine);
  or or_10 (D, Zero, Two, Three, Five, Six, Eight, Nine);
  or or_11 (E, Zero, Two, Six, Eight);
  or or_12 (F, Six, Four, Five, Eight, Nine, Zero);
  or or_13 (G, Two, Three, Four, Five, Six, Eight, Nine);
endmodule
